// Logisim project micro.circ as structural Verilog: 1 circuit, main circuit EV20_Superescalar
module EV20_Superescalar (
  input  in_1
);

  wire ALUALULAU_cyout, and_1_out, bloque1_1_preload, CLK, CLK2, CLK3, CLK4, dipswitch_1_sw1, LoadStore_p6,
       LoadStore_p7, LoadStore_p8, LoadStore_p9, LoadStore_p10, LoadStore_p11, LoadStore_p12, LoadStore_p13,
       LoadStore_p14, not_1_out, not_2_out, not_3_out, pipeline_register_1_p7, pipeline_register_1_p8,
       pipeline_register_1_p9, pipeline_register_1_p10, pipeline_register_1_p11, pipeline_register_1_p12,
       pipeline_register_1_p13, pipeline_register_1_p14, pipeline_register_2_p12, pipeline_register_2_p13,
       pipeline_register_2_p14, pipeline_register_2_p15, pipeline_register_2_p16, pipeline_register_2_p17,
       pipeline_register_2_p18, pipeline_register_2_p19, pipeline_register_2_p20, pipeline_register_2_p21,
       selector_a_1_p2, UC1_ALU_EN, UC1_LS_EN, undriven, undriven_2;
  wire [3:0] pipeline_register_1_p6;
  wire [5:0] selector_c_1_busc_selector;
  wire [9:0] UC1_ALU_DADRES, UC1_LS_DADRES;
  wire [10:0] ProgramCounterReg_ia0ia10;
  wire [14:0] MicroInstructionROM_microinstruction;
  wire [15:0] ALUALULAU_z, BusA_ALU_q, BusB_ALU_q;
  wire [23:0] BBUS, ProgramMemory_data;
  wire [30:0] UC1_ALU_SD, UC1_LS_SD;

  // Probe on ProgramCounterReg_ia0ia10
  ROM #(.addrWidth(11), .dataWidth(24)) ProgramMemory (.addr(ProgramCounterReg_ia0ia10), .data(ProgramMemory_data));
  Bloque1 bloque1_1 (.B12B11(BBUS[21:20]), .Preload(bloque1_1_preload));  // open: WRegister, CY
  and and_1 (and_1_out, bloque1_1_preload, BBUS[22]);
  PCreg ProgramCounterReg (
    .Preload(and_1_out), .CLK1(CLK), .HOLD(undriven), .B0B10(BBUS[15:5]), .IA0IA10(ProgramCounterReg_ia0ia10));
  Register #(.width(24)) InstructionRegister (.D(ProgramMemory_data), .en(undriven), .clk(CLK), .Q(BBUS));  // open: clr
  // Probe on BBUS
  not not_1 (not_1_out, UC1_ALU_EN);
  // Selector_A selector_a_1: pin names not known; wires that end beside it: BBUS, selector_a_1_p2
  // Pipeline_register pipeline_register_1: pin names not known; wires that end beside it: 1'b0, CLK3, UC1_ALU_SD, UC1_ALU_DADRES, not_1_out, pipeline_register_1_p6, pipeline_register_1_p7, pipeline_register_1_p8, pipeline_register_1_p9, pipeline_register_1_p10, pipeline_register_1_p11, pipeline_register_1_p12, pipeline_register_1_p13, pipeline_register_1_p14
  // Probe on pipeline_register_1_p7
  // Probe on pipeline_register_1_p8
  // Probe on pipeline_register_1_p9
  // Probe on pipeline_register_1_p10
  // Probe on pipeline_register_1_p11
  // Probe on pipeline_register_1_p12
  // Probe on pipeline_register_1_p13
  // Probe on pipeline_register_1_p14
  Selector_C selector_c_1 (.BusB(BBUS), .BusC_Selector(selector_c_1_busc_selector));
  // Probe on pipeline_register_1_p6
  Micro_Instruction_ROM MicroInstructionROM (
    .Instruction(BBUS), .MicroInstruction(MicroInstructionROM_microinstruction));
  Register #(.width(16)) BusA_ALU (.D(16'h1), .en(UC1_ALU_EN), .clk(CLK2), .Q(BusA_ALU_q));  // open: clr
  Register #(.width(16)) BusB_ALU (.D(16'h2), .en(UC1_ALU_EN), .clk(CLK2), .Q(BusB_ALU_q));  // open: clr
  not not_2 (not_2_out, undriven_2);
  // Probe on pipeline_register_2_p12
  // Pipeline_register pipeline_register_2: pin names not known; wires that end beside it: MicroInstructionROM_microinstruction[14:11], MicroInstructionROM_microinstruction[10:9], MicroInstructionROM_microinstruction[8], 1'b1, CLK2, MicroInstructionROM_microinstruction[7:6], BBUS[14:10], MicroInstructionROM_microinstruction[5:0], selector_c_1_busc_selector, selector_a_1_p2, BBUS[14:5], pipeline_register_2_p12, pipeline_register_2_p13, pipeline_register_2_p14, pipeline_register_2_p15, pipeline_register_2_p16, pipeline_register_2_p17, pipeline_register_2_p18, pipeline_register_2_p19, pipeline_register_2_p20, pipeline_register_2_p21
  // Probe on pipeline_register_2_p13
  // Probe on pipeline_register_2_p14
  // Probe on pipeline_register_2_p15
  // Probe on pipeline_register_2_p16
  // Probe on pipeline_register_2_p17
  // Probe on pipeline_register_2_p18
  // Probe on pipeline_register_2_p20
  // Probe on ALUALULAU_z
  ALU ALUALULAU (
    .ALUC(pipeline_register_1_p6), .A(BusA_ALU_q), .B(BusB_ALU_q), .Z(ALUALULAU_z), .CYout(ALUALULAU_cyout));  // open: CYin
  // Probe on ALUALULAU_cyout
  Pipeline_register pipeline_register_3 (
    .S_low_P_high(1'b0), .Hold(not_2_out));  // open: ALUC_IN, SH_IN, Kmx_IN, CLK, MRyMB_IN, B_bus_IN, T_bus_IN, C_bus_IN, Serial_IN, A_bus_IN, D_Address_IN, ALUC_OUT, SH_OUT, Kmx_OUT, MRyMB_OUT, B_bus_OUT, T_bus_OUT, C_bus_OUT, Serial_OUT, A_bus_OUT, D_Address_OUT
  // UC1 uc1_1: pin names not known; wires that end beside it: pipeline_register_2_p19, pipeline_register_2_p21, UC1_ALU_EN, UC1_LS_EN, UC1_ALU_SD, UC1_LS_SD, UC1_ALU_DADRES
  not not_3 (not_3_out, UC1_LS_EN);
  DipSwitch #(.number(2)) dipswitch_1 (.sw1(dipswitch_1_sw1));  // open: sw2
  Register #(.width(16)) BusA_LS (.D(16'haaaa), .en(UC1_LS_EN), .clk(CLK2));  // open: Q, clr
  ClockGenerator clocks (.Auto(dipswitch_1_sw1), .ManualCLK(in_1), .CLK(CLK), .CLK2(CLK2), .CLK3(CLK3), .CLK4(CLK4));
  // Pipeline_register LoadStore: pin names not known; wires that end beside it: 1'b0, CLK3, UC1_LS_SD, UC1_LS_DADRES, not_3_out, LoadStore_p6, LoadStore_p7, LoadStore_p8, LoadStore_p9, LoadStore_p10, LoadStore_p11, LoadStore_p12, LoadStore_p13, LoadStore_p14
  // Data data_1: pin names not known
  // Probe on LoadStore_p6
  // Probe on LoadStore_p7
  // Probe on LoadStore_p8
  // Probe on LoadStore_p9
  // Probe on LoadStore_p10
  // Probe on LoadStore_p11
  // Probe on LoadStore_p12
  // Probe on LoadStore_p13
  // Probe on LoadStore_p14

  // Other names for the same wires on the sheet: pulseGenManual = in_1

  // Notes on the sheet:
  //   contents of ProgramMemory (hex, n*v repeats v):
  //   400140
  //   BUS B
endmodule
